# Fritzing sketch schematic (saved by Fritzing 0.9.10b)
breadboards: 1

parts:
  Q1 = NPN-Transistor [package="TO92 [THT]"]
  Part1 = Arduino Uno (Rev3)
  R1 = Resistor [tolerance=±5% power=0.25 resistance=220 package=THT]
  U1 = Vibration Motor- ROB-08449 [package=vibe-motor-10mm]

nets:
  N1: Q1.E, Part1.GND
  N2: Q1.B, R1.Pin_1
  N3: Q1.C, U1.+
  N4: Part1.D3_PWM, R1.Pin_0
  N5: Part1.3V3, U1.-
